# Fritzing sketch iSpindel (saved by Fritzing 0.9.3b)

parts:
  WeMos_D1_Mini1 = WeMos D1 Mini
  TP1 = TP4056 [chip_label=TP4056 package="DIP (Dual Inline) [THT]"]
  DS1 = DS18B20 1-Wire Temperature Sensor [part_number=DS18B20]
  Bauteil1 = InvenSense MPU6050
  R1 = Resistor [tolerance=±5% resistance=4.7k package="1206 [SMD]"]
  R2 = Resistor [tolerance=±5% resistance=390 package="1206 [SMD]"]
  R3 = Resistor [tolerance=±5% resistance=220k package="1206 [SMD]"]
  S2 = Toggle Switch [package=THT]
  BAT2 = Battery Holders [package=lipo-1100mAh]

nets:
  5V: WeMos_D1_Mini1.5V, DS1.VDD, Bauteil1.VCC, R1.Pin_0
  N1: WeMos_D1_Mini1.A0, R3.Pin_1
  N2: WeMos_D1_Mini1.D0, R2.Pin_1
  N3: WeMos_D1_Mini1.D3, Bauteil1.SDA
  N4: WeMos_D1_Mini1.D4, Bauteil1.SCL
  N5: WeMos_D1_Mini1.D6, DS1.DQ
  N6: WeMos_D1_Mini1.G, Bauteil1.GND
  N7: WeMos_D1_Mini1.RST, R2.Pin_0
  N8: TP1.pin3, S2.L2
  N9: TP1.pin4, BAT2.+
  N10: TP1.pin5, BAT2.-

notes:
  R1 4,7K
  R2 220K
  R3 390
  Die Diode am D1mini muss netfernt werde, da sonst das Modul beim Laden kaputt gehen kann.

custom parts:
  WeMos D1 Mini: The D1 mini is a mini wifi board based on ESP-8266EX.
  TP4056: A DIP stand-in part for whatever IC you want. With 6 pins on a 300mil dual inline package (DIP) footprint.
